// Logisim project control_logic.circ as structural Verilog: 1 circuit, main circuit control_logic
module control_logic (
  input  [31:0] inst,
  input  BrEq,
  input  BrLt,
  output PCSel,
  output RegWEn,
  output [2:0] ImmSel,
  output BrUn,
  output ASel,
  output BSel,
  output [3:0] ALUSel,
  output MemRW,
  output [1:0] WBSel,
  output CSRSel,
  output CSRWen,
  output lb,
  output lh,
  output sb,
  output sh
);

  wire and_1_out, and_12_out, and_13_out, and_14_out, and_15_out, comparator_1_eq, comparator_2_eq,
       comparator_3_eq, comparator_4_eq, comparator_5_eq, comparator_6_eq, comparator_7_eq, comparator_8_eq,
       comparator_9_eq, comparator_10_eq, comparator_11_eq, comparator_12_eq, comparator_13_eq,
       comparator_14_eq, comparator_15_eq, comparator_16_eq, comparator_20_eq, comparator_21_eq,
       comparator_22_eq, comparator_23_eq, comparator_24_eq, comparator_30_eq, comparator_31_eq,
       comparator_33_eq, comparator_34_eq, comparator_35_eq, comparator_36_eq, is_auipc, is_beq, is_bge,
       is_bgeu, is_blt, is_bltu, is_bnq, is_csrw, is_I, is_jalr, is_load, is_lui, is_mul, is_mulh, is_R,
       is_SB, is_sra, is_sub, is_U, is_UJ, nor_1_out, not_1_out, not_2_out, not_3_out, not_4_out, not_5_out,
       not_6_out, or_2_out, or_3_out, or_4_out, or_7_out, or_8_out, or_11_out, satisfied;
  wire [1:0] multiplexer_7_out, multiplexer_9_out;
  wire [2:0] multiplexer_11_out, multiplexer_12_out, multiplexer_13_out, multiplexer_14_out;
  wire [3:0] multiplexer_1_out, multiplexer_2_out, multiplexer_3_out, multiplexer_4_out, multiplexer_6_out,
       RIsel;

  not not_1 (not_1_out, BrEq);
  not not_2 (not_2_out, BrLt);
  Comparator #(.width(3)) comparator_1 (.a(inst[14:12]), .b(3'b000), .eq(comparator_1_eq));  // open: gt, lt
  Comparator #(.width(3)) comparator_2 (.a(inst[14:12]), .b(3'b100), .eq(comparator_2_eq));  // open: gt, lt
  and and_1 (and_1_out, not_1_out, not_2_out, is_SB);
  Comparator #(.width(3)) comparator_3 (.a(inst[14:12]), .b(3'b101), .eq(comparator_3_eq));  // open: gt, lt
  and and_2 (is_beq, comparator_1_eq, BrEq);
  not not_3 (not_3_out, is_beq);
  and and_3 (is_blt, comparator_2_eq, BrLt);
  not not_4 (not_4_out, is_blt);
  and and_4 (is_bgeu, and_1_out, not_5_out);
  and and_5 (is_bge, and_1_out, comparator_3_eq);
  and and_6 (is_bnq, not_3_out, BrEq);
  and and_7 (is_bltu, not_4_out, BrLt);
  not not_5 (not_5_out, is_bge);
  Comparator #(.width(3)) comparator_4 (.a(inst[14:12]), .b(3'b000), .eq(comparator_4_eq));  // open: gt, lt
  Comparator #(.width(7)) comparator_5 (.a(inst[31:25]), .b(7'b0000001), .eq(comparator_5_eq));  // open: gt, lt
  Comparator #(.width(7)) comparator_6 (.a(inst[6:0]), .b(7'b0110011), .eq(comparator_6_eq));  // open: gt, lt
  Multiplexer #(.enable("false"), .select(3), .width(4)) multiplexer_1 (
    .in0(4'b0000), .in1(4'b0110), .in2(4'b0111), .in3(4'b1011), .in4(4'b0011), .in5(4'b0100), .in6(4'b0010),
    .in7(4'b0001), .out(multiplexer_1_out), .sel(inst[14:12]));
  and and_8 (is_mul, comparator_4_eq, comparator_5_eq, comparator_6_eq);
  or or_1 (CSRWen, is_csrw, CSRSel);
  Comparator #(.width(3)) comparator_7 (.a(inst[14:12]), .b(3'b110), .eq(comparator_7_eq));  // open: gt, lt
  Comparator #(.width(3)) comparator_8 (.a(inst[14:12]), .b(3'b111), .eq(comparator_8_eq));  // open: gt, lt
  Multiplexer #(.enable("false"), .width(4)) multiplexer_2 (
    .in0(multiplexer_1_out), .in1(4'b1010), .out(multiplexer_2_out), .sel(is_mul));
  or or_2 (or_2_out, comparator_7_eq, comparator_8_eq);
  Multiplexer #(.enable("false"), .width(4)) multiplexer_3 (
    .in0(multiplexer_2_out), .in1(4'b1100), .out(multiplexer_3_out), .sel(is_sub));
  and and_9 (BrUn, is_SB, or_2_out);
  Comparator #(.width(3)) comparator_9 (.a(inst[14:12]), .b(3'b000), .eq(comparator_9_eq));  // open: gt, lt
  Comparator #(.width(7)) comparator_10 (.a(inst[31:25]), .b(7'b0100000), .eq(comparator_10_eq));  // open: gt, lt
  Comparator #(.width(7)) comparator_11 (.a(inst[6:0]), .b(7'b0110011), .eq(comparator_11_eq));  // open: gt, lt
  and and_10 (is_sub, comparator_9_eq, comparator_10_eq, comparator_11_eq);
  Multiplexer #(.enable("false"), .width(4)) multiplexer_4 (
    .in0(multiplexer_3_out), .in1(4'b1110), .out(multiplexer_4_out), .sel(is_mulh));
  Comparator #(.width(3)) comparator_12 (.a(inst[14:12]), .b(3'b001), .eq(comparator_12_eq));  // open: gt, lt
  and and_11 (is_csrw, comparator_12_eq, comparator_13_eq);
  Comparator #(.width(7)) comparator_13 (.a(inst[6:0]), .b(7'b1110011), .eq(comparator_13_eq));  // open: gt, lt
  Multiplexer #(.enable("false"), .width(4)) multiplexer_5 (
    .in0(multiplexer_4_out), .in1(4'b0101), .out(RIsel), .sel(is_sra));
  not not_6 (not_6_out, BrEq);
  or or_3 (or_3_out, is_blt, is_bltu);
  Comparator #(.width(3)) comparator_14 (.a(inst[14:12]), .b(3'b001), .eq(comparator_14_eq));  // open: gt, lt
  Comparator #(.width(7)) comparator_15 (.a(inst[31:25]), .b(7'b0000001), .eq(comparator_15_eq));  // open: gt, lt
  Comparator #(.width(7)) comparator_16 (.a(inst[6:0]), .b(7'b0110011), .eq(comparator_16_eq));  // open: gt, lt
  and and_12 (and_12_out, BrEq, is_beq);
  and and_13 (and_13_out, not_6_out, is_bnq);
  and and_14 (and_14_out, BrLt, or_3_out);
  nor nor_1 (nor_1_out, BrEq, BrLt);
  or or_4 (or_4_out, is_bge, is_bgeu);
  or or_5 (RegWEn, is_R, is_I, is_U, is_UJ, is_jalr, is_csrw, CSRSel);
  and and_15 (and_15_out, nor_1_out, or_4_out);
  and and_16 (is_mulh, comparator_14_eq, comparator_15_eq, comparator_16_eq);
  Comparator #(.width(7)) comparator_17 (.a(inst[6:0]), .b(7'b0110011), .eq(is_R));  // open: gt, lt
  Comparator #(.width(7)) comparator_18 (.a(inst[6:0]), .b(7'b0010011), .eq(is_I));  // open: gt, lt
  or or_6 (satisfied, and_12_out, and_13_out, and_14_out, and_15_out);
  Multiplexer #(.enable("false"), .width(4)) multiplexer_6 (
    .in0(4'b0000), .in1(RIsel), .out(multiplexer_6_out), .sel(or_7_out));
  or or_7 (or_7_out, is_I, is_R);
  Multiplexer #(.enable("false"), .width(2)) multiplexer_7 (
    .in0(2'b01), .in1(2'b00), .out(multiplexer_7_out), .sel(is_load));
  or or_8 (or_8_out, is_UJ, is_jalr);
  or or_9 (PCSel, satisfied, is_UJ, is_jalr);
  Comparator #(.width(7)) comparator_19 (.a(inst[6:0]), .b(7'b0010111), .eq(is_auipc));  // open: gt, lt
  Comparator #(.width(3)) comparator_20 (.a(inst[14:12]), .b(3'b101), .eq(comparator_20_eq));  // open: gt, lt
  Comparator #(.width(7)) comparator_21 (.a(inst[31:25]), .b(7'b0100000), .eq(comparator_21_eq));  // open: gt, lt
  Comparator #(.width(7)) comparator_22 (.a(inst[6:0]), .b(7'b0110011), .eq(comparator_22_eq));  // open: gt, lt
  Multiplexer #(.enable("false"), .width(4)) multiplexer_8 (
    .in0(multiplexer_6_out), .in1(4'b1101), .out(ALUSel), .sel(is_lui));
  Multiplexer #(.enable("false"), .width(2)) multiplexer_9 (
    .in0(multiplexer_7_out), .in1(2'b10), .out(multiplexer_9_out), .sel(or_8_out));
  or or_10 (ASel, is_SB, is_UJ, is_auipc);
  and and_17 (is_sra, comparator_20_eq, comparator_21_eq, comparator_22_eq);
  Multiplexer #(.enable("false"), .width(2)) multiplexer_10 (
    .in0(multiplexer_9_out), .in1(2'b11), .out(WBSel), .sel(or_11_out));
  or or_11 (or_11_out, is_csrw, CSRSel);
  Comparator #(.width(3)) comparator_23 (.a(inst[14:12]), .b(3'b000), .eq(comparator_23_eq));  // open: gt, lt
  Comparator #(.width(3)) comparator_24 (.a(inst[14:12]), .b(3'b000), .eq(comparator_24_eq));  // open: gt, lt
  Comparator #(.width(7)) comparator_25 (.a(inst[6:0]), .b(7'b0000011), .eq(is_load));  // open: gt, lt
  Comparator #(.width(7)) comparator_26 (.a(inst[6:0]), .b(7'b0110111), .eq(is_lui));  // open: gt, lt
  Comparator #(.width(7)) comparator_27 (.a(inst[6:0]), .b(7'b1100111), .eq(is_jalr));  // open: gt, lt
  Comparator #(.width(7)) comparator_28 (.a(inst[6:0]), .b(7'b0100011), .eq(MemRW));  // open: gt, lt
  Comparator #(.width(7)) comparator_29 (.a(inst[6:0]), .b(7'b1100011), .eq(is_SB));  // open: gt, lt
  Comparator #(.width(7)) comparator_30 (.a(inst[6:0]), .b(7'b0010111), .eq(comparator_30_eq));  // open: gt, lt
  Comparator #(.width(7)) comparator_31 (.a(inst[6:0]), .b(7'b0110111), .eq(comparator_31_eq));  // open: gt, lt
  Comparator #(.width(7)) comparator_32 (.a(inst[6:0]), .b(7'b1101111), .eq(is_UJ));  // open: gt, lt
  Comparator #(.width(7)) comparator_33 (.a(inst[6:0]), .b(7'b1110011), .eq(comparator_33_eq));  // open: gt, lt
  Comparator #(.width(3)) comparator_34 (.a(inst[14:12]), .b(3'b101), .eq(comparator_34_eq));  // open: gt, lt
  and and_18 (lb, is_load, comparator_23_eq);
  and and_19 (sb, MemRW, comparator_24_eq);
  or or_12 (is_U, comparator_30_eq, comparator_31_eq);
  and and_20 (CSRSel, comparator_33_eq, comparator_34_eq);
  Comparator #(.width(3)) comparator_35 (.a(inst[14:12]), .b(3'b001), .eq(comparator_35_eq));  // open: gt, lt
  Comparator #(.width(3)) comparator_36 (.a(inst[14:12]), .b(3'b001), .eq(comparator_36_eq));  // open: gt, lt
  Multiplexer #(.enable("false"), .width(3)) multiplexer_11 (
    .in0(3'b000), .in1(3'b001), .out(multiplexer_11_out), .sel(MemRW));
  and and_21 (lh, is_load, comparator_35_eq);
  and and_22 (sh, is_load, comparator_36_eq);
  or or_13 (BSel, is_load, is_I, is_SB, is_U, is_UJ, is_jalr);
  Multiplexer #(.enable("false"), .width(3)) multiplexer_12 (
    .in0(multiplexer_11_out), .in1(3'b010), .out(multiplexer_12_out), .sel(is_SB));
  Multiplexer #(.enable("false"), .width(3)) multiplexer_13 (
    .in0(multiplexer_12_out), .in1(3'b011), .out(multiplexer_13_out), .sel(is_U));
  Multiplexer #(.enable("false"), .width(3)) multiplexer_14 (
    .in0(multiplexer_13_out), .in1(3'b100), .out(multiplexer_14_out), .sel(is_UJ));
  Multiplexer #(.enable("false"), .width(3)) multiplexer_15 (
    .in0(multiplexer_14_out), .in1(3'b101), .out(ImmSel), .sel(CSRSel));

  // Other names for the same wires on the sheet: opcode[6:0] = inst[6:0]; funct3[2:0] = inst[14:12];
  //   funct7[6:0] = inst[31:25]; is_csrwi = CSRSel; is_S = MemRW

  // Notes on the sheet:
  //   Instruction Decode
  //   INPUTS to your circuit
  //   judge the type of Branch
  //   is BrGt
  //   DON'T CHANGE THE LOCATIONS OF THE INPUTS AND OUTPUTS!
  //   OUTPUT from your circuit
  //   MemRW
  //   CSRSel & CSRWen
  //   BrUn
  //   ALUSel
  //   RegWEn
  //   其他指令默认为add
  //   PCSel
  //   ASel
  //   WBSel
  //   BSel
  //   load & store type
  //   ImmSel
endmodule
