// Logisim project cpu.circ as structural Verilog: 1 circuit, main circuit cpu
module cpu (
  input  clk,
  input  [31:0] INSTRUCTION,
  input  [31:0] READ_DATA,
  output [31:0] WRITE_ADDRESS,
  output [31:0] PROGRAM_COUNTER,
  output [31:0] ra,
  output [31:0] sp,
  output [31:0] t0,
  output [31:0] t1,
  output [31:0] t2,
  output [31:0] s0,
  output [31:0] s1,
  output [31:0] a0,
  output [31:0] tohost,
  output [3:0] WRITE_ENABLE,
  output [31:0] WRITE_DATA
);

  wire ASel, BrEq, BrLt, BrUn, BSel, CSRSel, CSRWen, lb, lh, lw, MemRW, PCSel, RegWEn, sb, sh, sw;
  wire [1:0] WBSel;
  wire [2:0] ImmSel;
  wire [3:0] ALUSel, multiplexer_6_out, multiplexer_7_out;
  wire [31:0] adder_1_out, adder_2_out, bit_extender_1_out, bit_extender_2_out, Imm, INSTRUCTION2,
       multiplexer_1_out, multiplexer_2_out, multiplexer_3_out, multiplexer_4_out, multiplexer_5_out,
       multiplexer_8_out, PC_ID, read_data1, READ_DATA2, WBdata;

  Adder #(.width(32)) adder_1 (.a(PROGRAM_COUNTER), .b(32'h4), .out(adder_1_out));  // open: cin, cout
  Multiplexer #(.enable("false"), .width(32)) multiplexer_1 (
    .in0(adder_1_out), .in1(WRITE_ADDRESS), .out(multiplexer_1_out), .sel(PCSel));
  Register #(.width(32)) PC_IF (.D(multiplexer_1_out), .clk(clk), .Q(PROGRAM_COUNTER));  // open: en, clr
  Register #(.width(32)) register_1 (.D(multiplexer_2_out), .clk(clk), .Q(INSTRUCTION2));  // open: en, clr
  Multiplexer #(.enable("false"), .width(32)) multiplexer_2 (
    .in0(INSTRUCTION), .in1(32'h13), .out(multiplexer_2_out), .sel(PCSel));
  Register #(.width(32)) u_PC_ID (.D(PROGRAM_COUNTER), .clk(clk), .Q(PC_ID));  // open: en, clr
  // control_logic control_logic_1: pin names not known; wires that end beside it: sb, sh, sw, lb, lh, lw, INSTRUCTION2, PCSel, RegWEn, ImmSel, BrEq, BrLt, BrUn, ASel, BSel, ALUSel, MemRW, WBSel, CSRSel, CSRWen
  imm_gen imm_gen_1 (.inst(INSTRUCTION2), .ImmSel(ImmSel), .imm(Imm));
  regfile_main main_1 (
    .s1(s1), .a0(a0), .Read_Data_1(read_data1), .Read_Data_2(WRITE_DATA), .ra(ra), .sp(sp), .t0(t0), .t1(t1),
    .t2(t2), .s0(s0), .RegWEn(RegWEn), .clk(clk), .Write_Data(WBdata), .rs1(INSTRUCTION[19:15]),
    .rs2(INSTRUCTION[24:20]), .rd(INSTRUCTION[11:7]));
  Multiplexer #(.enable("false"), .width(32)) multiplexer_3 (
    .in0(read_data1), .in1(Imm), .out(multiplexer_3_out), .sel(CSRSel));
  Multiplexer #(.enable("false"), .width(32)) multiplexer_4 (
    .in0(read_data1), .in1(PC_ID), .out(multiplexer_4_out), .sel(ASel));
  Multiplexer #(.enable("false"), .width(32)) multiplexer_5 (
    .in0(WRITE_DATA), .in1(Imm), .out(multiplexer_5_out), .sel(BSel));
  // csr csr_1: pin names not known; wires that end beside it: 12'h51e, multiplexer_3_out, CSRWen, clk, tohost
  // alu alu_1: pin names not known; wires that end beside it: multiplexer_4_out, multiplexer_5_out, ALUSel, WRITE_ADDRESS
  branch_comp branch_comp_1 (.rs1(read_data1), .rs2(WRITE_DATA), .BrUn(BrUn), .BrEq(BrEq), .BrLt(BrLt));
  Adder #(.width(32)) adder_2 (.a(PC_ID), .b(32'h4), .out(adder_2_out));  // open: cin, cout
  Multiplexer #(.enable("false"), .width(4)) multiplexer_6 (
    .in0(4'b1111), .in1(4'b0011), .out(multiplexer_6_out), .sel(sh));
  assign bit_extender_1_out = {{24{READ_DATA[7]}}, READ_DATA[7:0]};  // Bit_Extender bit_extender_1
  assign bit_extender_2_out = {{16{READ_DATA[15]}}, READ_DATA[15:0]};  // Bit_Extender bit_extender_2
  Multiplexer #(.enable("false"), .width(4)) multiplexer_7 (
    .in0(multiplexer_6_out), .in1(4'b0001), .out(multiplexer_7_out), .sel(sb));
  Multiplexer #(.enable("false"), .width(32)) multiplexer_8 (
    .in0(READ_DATA), .in1(bit_extender_1_out), .out(multiplexer_8_out), .sel(lb));
  Multiplexer #(.enable("false"), .select(2), .width(32)) multiplexer_9 (
    .in0(READ_DATA2), .in1(WRITE_ADDRESS), .in2(adder_2_out), .in3(Imm), .out(WBdata), .sel(WBSel));
  Multiplexer #(.enable("false"), .width(4)) multiplexer_10 (
    .in0(4'b0000), .in1(multiplexer_7_out), .out(WRITE_ENABLE), .sel(MemRW));
  Multiplexer #(.enable("false"), .width(32)) multiplexer_11 (
    .in0(multiplexer_8_out), .in1(bit_extender_2_out), .out(READ_DATA2), .sel(lh));

  // Other names for the same wires on the sheet: ALU_output[31:0] = WRITE_ADDRESS; opcode[6:0] = INSTRUCTION[6:0];
  //   rd[4:0] = INSTRUCTION[11:7]; funct3[2:0] = INSTRUCTION[14:12]; rs1[4:0] = INSTRUCTION[19:15];
  //   rs2[4:0] = INSTRUCTION[24:20]; funct7[6:0] = INSTRUCTION[31:25]; read_data2_t[31:0] = WRITE_DATA

  // Notes on the sheet:
  //   NOP
  //   Output to IMEM
  //   IMEM (do **NOT** move this)
  //   Inputs from IMEM
  //   decode
  //   It is OK to move the PC, RegFile, ALU, MEM, Branch Comp, Imm Gen, and Control Logic to wherever is most convenient for you when constructing your CPU, and to delete this text
  //   Inputs/Outputs for testing. Do **NOT** move these.
  //   Outputs To DMEM
  //   DMEM (do **NOT** move this)
  //   Inputs From DMEM
endmodule
